// Logisim project CPU_I.circ as structural Verilog: 2 circuits, main circuit main
module main (
  input  in_1,
  input  [23:0] in_2
);

  wire button_1_out, clock_1_out, comparator_1_eq;
  wire [3:0] pull_resistor_1_node, rom_1_data_2, rom_1_data_3;
  wire [23:0] counter_1_q, rom_1_data;

  Clock clock_1 (.out(clock_1_out));
  Button button_1 (.out(button_1_out));
  Counter #(.max('hffffff), .width(24)) counter_1 (
    .load(in_1), .D(in_2), .count(1'b1), .Q(counter_1_q), .up(1'b1), .clk(clock_1_out), .clr(button_1_out));  // open: carry
  ROM #(.addrWidth(24), .dataWidth(32)) rom_1 (.addr(counter_1_q), .data({rom_1_data_3, rom_1_data_2, rom_1_data}));
  Comparator #(.width(4)) comparator_1 (.a(rom_1_data_3), .b(4'b0001), .eq(comparator_1_eq));  // open: gt, lt
  RegisterBank registerbank_1 (
    .RB_CLK(clock_1_out), .ReadA(rom_1_data[19:16]), .ReadB(rom_1_data[15:12]), .Target(rom_1_data[23:20]),
    .RB_RST(button_1_out));  // open: DataIn, SourceA, SourceB
  Pull_Resistor pull_resistor_1 (.node(pull_resistor_1_node));
  assign pull_resistor_1_node = comparator_1_eq ? rom_1_data_2 : 4'bz;  // Controlled_Buffer controlled_buffer_1
  Pull_Resistor pull_resistor_2 (.node(rom_1_data_2));

  // Notes on the sheet:
  //   contents of rom_1 (hex, n*v repeats v):
  //   15*0 12000000
endmodule

module RegisterBank (
  input  RB_CLK,
  input  [31:0] DataIn,
  input  [3:0] ReadA,
  input  [3:0] ReadB,
  input  [3:0] Target,
  input  RB_RST,
  output [31:0] SourceA,
  output [31:0] SourceB
);

  wire decoder_1_out1, decoder_1_out2, decoder_1_out3, decoder_1_out4, decoder_1_out5, decoder_1_out6,
       decoder_1_out7, decoder_1_out8, decoder_1_out9, decoder_1_out10, decoder_1_out11, decoder_1_out12,
       decoder_1_out13, decoder_1_out14, decoder_1_out15;
  wire [31:0] register_1_q, register_2_q, register_3_q, register_4_q, register_5_q, register_6_q,
       register_7_q, register_8_q, register_9_q, register_10_q, register_11_q, register_12_q, register_13_q,
       register_14_q, register_15_q;

  Decoder #(.enable("false"), .select(4)) decoder_1 (
    .out1(decoder_1_out1), .out2(decoder_1_out2), .out3(decoder_1_out3), .out4(decoder_1_out4),
    .out5(decoder_1_out5), .out6(decoder_1_out6), .out7(decoder_1_out7), .out8(decoder_1_out8),
    .out9(decoder_1_out9), .out10(decoder_1_out10), .out11(decoder_1_out11), .out12(decoder_1_out12),
    .out13(decoder_1_out13), .out14(decoder_1_out14), .out15(decoder_1_out15), .sel(Target));  // open: out0
  Register #(.width(32)) register_1 (.D(DataIn), .en(decoder_1_out1), .clk(RB_CLK), .Q(register_1_q), .clr(RB_RST));
  Register #(.width(32)) register_2 (.D(DataIn), .en(decoder_1_out2), .clk(RB_CLK), .Q(register_2_q), .clr(RB_RST));
  Register #(.width(32)) register_3 (.D(DataIn), .en(decoder_1_out3), .clk(RB_CLK), .Q(register_3_q), .clr(RB_RST));
  Register #(.width(32)) register_4 (.D(DataIn), .en(decoder_1_out4), .clk(RB_CLK), .Q(register_4_q), .clr(RB_RST));
  Register #(.width(32)) register_5 (.D(DataIn), .en(decoder_1_out5), .clk(RB_CLK), .Q(register_5_q), .clr(RB_RST));
  Register #(.width(32)) register_6 (.D(DataIn), .en(decoder_1_out6), .clk(RB_CLK), .Q(register_6_q), .clr(RB_RST));
  Register #(.width(32)) register_7 (.D(DataIn), .en(decoder_1_out7), .clk(RB_CLK), .Q(register_7_q), .clr(RB_RST));
  Register #(.width(32)) register_8 (.D(DataIn), .en(decoder_1_out8), .clk(RB_CLK), .Q(register_8_q), .clr(RB_RST));
  Register #(.width(32)) register_9 (.D(DataIn), .en(decoder_1_out9), .clk(RB_CLK), .Q(register_9_q), .clr(RB_RST));
  Register #(.width(32)) register_10 (.D(DataIn), .en(decoder_1_out10), .clk(RB_CLK), .Q(register_10_q), .clr(RB_RST));
  Register #(.width(32)) register_11 (.D(DataIn), .en(decoder_1_out11), .clk(RB_CLK), .Q(register_11_q), .clr(RB_RST));
  Register #(.width(32)) register_12 (.D(DataIn), .en(decoder_1_out12), .clk(RB_CLK), .Q(register_12_q), .clr(RB_RST));
  Register #(.width(32)) register_13 (.D(DataIn), .en(decoder_1_out13), .clk(RB_CLK), .Q(register_13_q), .clr(RB_RST));
  Register #(.width(32)) register_14 (.D(DataIn), .en(decoder_1_out14), .clk(RB_CLK), .Q(register_14_q), .clr(RB_RST));
  Register #(.width(32)) register_15 (.D(DataIn), .en(decoder_1_out15), .clk(RB_CLK), .Q(register_15_q), .clr(RB_RST));
  Multiplexer #(.select(4), .width(32)) multiplexer_1 (
    .in0({32{1'b0}}), .in1(register_1_q), .in2(register_2_q), .in3(register_3_q), .in4(register_4_q),
    .in5(register_5_q), .in6(register_6_q), .in7(register_7_q), .in8(register_8_q), .in9(register_9_q),
    .in10(register_10_q), .in11(register_11_q), .in12(register_12_q), .in13(register_13_q),
    .in14(register_14_q), .in15(register_15_q), .out(SourceA), .sel(ReadA));
  Multiplexer #(.select(4), .width(32)) multiplexer_2 (
    .in0({32{1'b0}}), .in1(register_1_q), .in2(register_2_q), .in3(register_3_q), .in4(register_4_q),
    .in5(register_5_q), .in6(register_6_q), .in7(register_7_q), .in8(register_8_q), .in9(register_9_q),
    .in10(register_10_q), .in11(register_11_q), .in12(register_12_q), .in13(register_13_q),
    .in14(register_14_q), .in15(register_15_q), .out(SourceB), .sel(ReadB));
endmodule
